# Fritzing sketch Second_montage_raspberry_avec_pull_up (saved by Fritzing 0.9.2b)
breadboards: 1

parts:
  Raspberry_Pi1 = Raspberry Pi 2
  R1 = Resistor [tolerance=±5% resistance=220 package=THT]
  LED1 = LED - 5mm [color="Red (633nm)" package="5 mm [THT]"]
  S1 = Pushbutton [package="[THT]"]
  R2 = Resistor [tolerance=±5% resistance=100k package=THT]

nets:
  N1: Raspberry_Pi1.3v3, R2.Pin_1
  N2: Raspberry_Pi1.GPIO4, S1.Pin_1, S1.Pin_2, R2.Pin_0
  N3: Raspberry_Pi1.GPIO26, R1.Pin_1
  N4: Raspberry_Pi1.GND, LED1.cathode, S1.Pin_3, S1.Pin_4
  N5: R1.Pin_0, LED1.anode
